// Logisim project Calculadora Digital.circ as structural Verilog: 16 circuits, main circuit main
module main (
  input  [3:0] A,
  input  [3:0] B,
  input  Limpar,
  input  Registrar,
  input  Registrar_2,
  input  Limpar_2,
  input  [1:0] in_7,
  output [7:0] out_8
);

  wire [3:0] register_1_q, register_2_q;
  wire [6:0] decodificador_binario_7_seg_1_s0, decodificador_binario_7_seg_1_s1,
       decodificador_binario_7_seg_1_s2;
  wire [7:0] register_3_q;

  Register #(.width(4)) register_1 (.D(A), .Q(register_1_q), .clk(Registrar), .clr(Limpar_2));  // open: en
  Register #(.width(4)) register_2 (.D(B), .Q(register_2_q), .clk(Registrar), .clr(Limpar_2));  // open: en
  calculadora calculadora (.A(register_1_q), .B(register_2_q), .\Operação (in_7), .Resultado(out_8));
  Register register_3 (.D(out_8), .Q(register_3_q), .clk(Registrar_2), .clr(Limpar));  // open: en
  decodificador_binario_7_seg decodificador_binario_7_seg_1 (
    .Entrada(register_3_q), .S0(decodificador_binario_7_seg_1_s0), .S1(decodificador_binario_7_seg_1_s1),
    .S2(decodificador_binario_7_seg_1_s2));
  _7_Segment_Display u_7_segment_display_1 (
    .g(decodificador_binario_7_seg_1_s2[3]), .f(decodificador_binario_7_seg_1_s2[2]),
    .a(decodificador_binario_7_seg_1_s2[1]), .b(decodificador_binario_7_seg_1_s2[0]),
    .e(decodificador_binario_7_seg_1_s2[4]), .d(decodificador_binario_7_seg_1_s2[5]),
    .c(decodificador_binario_7_seg_1_s2[6]), .dp(1'b0));
  _7_Segment_Display u_7_segment_display_2 (
    .g(decodificador_binario_7_seg_1_s1[3]), .f(decodificador_binario_7_seg_1_s1[2]),
    .a(decodificador_binario_7_seg_1_s1[1]), .b(decodificador_binario_7_seg_1_s1[0]),
    .e(decodificador_binario_7_seg_1_s1[4]), .d(decodificador_binario_7_seg_1_s1[5]),
    .c(decodificador_binario_7_seg_1_s1[6]), .dp(1'b0));
  _7_Segment_Display u_7_segment_display_3 (
    .g(decodificador_binario_7_seg_1_s0[3]), .f(decodificador_binario_7_seg_1_s0[2]),
    .a(decodificador_binario_7_seg_1_s0[1]), .b(decodificador_binario_7_seg_1_s0[0]),
    .e(decodificador_binario_7_seg_1_s0[4]), .d(decodificador_binario_7_seg_1_s0[5]),
    .c(decodificador_binario_7_seg_1_s0[6]), .dp(1'b0));
endmodule

module somador (
  input  [3:0] A,
  input  [3:0] B,
  output Carry,
  output [3:0] S
);

  wire meio_somador_carry;

  meio_somador meio_somador (.A(A[0]), .B(B[0]), .Soma(S[0]), .Carry(meio_somador_carry));
  somador_3_bits somador_3_bits (
    .A1(A[1]), .A2(A[2]), .A3(A[3]), .B1(B[1]), .B2(B[2]), .B3(B[3]), .Carry_in(meio_somador_carry),
    .Carry(Carry), .S1(S[1]), .S2(S[2]), .S3(S[3]));
endmodule

module multiplexador (
  input  in_1,
  input  in_2,
  input  in_3,
  output out_4
);

  // OR_Gate or_1 has open pins: out=out_4
endmodule

module meio_somador (
  input  A,
  input  B,
  output Soma,
  output Carry
);

  xor xor_1 (Soma, A, B);
  and and_1 (Carry, A, B);
endmodule

module subtrator (
  input  [3:0] A,
  input  [3:0] B,
  output Carry,
  output [3:0] S
);

  wire not_1_out, not_2_out, not_3_out, not_4_out, somador_completo_1_carry;

  somador_completo somador_completo_1 (
    .A(A[0]), .B(not_1_out), .Cin(1'b1), .Soma(S[0]), .Carry(somador_completo_1_carry));
  not not_1 (not_1_out, B[0]);
  not not_2 (not_2_out, B[1]);
  not not_3 (not_3_out, B[2]);
  not not_4 (not_4_out, B[3]);
  somador_3_bits somador_3_bits_1 (
    .A1(A[1]), .A2(A[2]), .A3(A[3]), .B1(not_2_out), .B2(not_3_out), .B3(not_4_out),
    .Carry_in(somador_completo_1_carry), .Carry(Carry), .S1(S[1]), .S2(S[2]), .S3(S[3]));
endmodule

module somador_completo (
  input  A,
  input  B,
  input  Cin,
  output Soma,
  output Carry
);

  wire and_1_out, and_2_out, xor_1_out;

  xor xor_1 (xor_1_out, A, B);
  xor xor_2 (Soma, Cin, xor_1_out);
  and and_1 (and_1_out, xor_1_out, Cin);
  and and_2 (and_2_out, A, B);
  or or_1 (Carry, and_1_out, and_2_out);
endmodule

module somador_3_bits (
  input  A1,
  input  A2,
  input  A3,
  input  B1,
  input  B2,
  input  B3,
  input  Carry_in,
  output Carry,
  output S1,
  output S2,
  output S3
);

  wire somador_completo_2_carry, somador_completo_carry;

  somador_completo somador_completo (.A(A1), .B(B1), .Cin(Carry_in), .Soma(S1), .Carry(somador_completo_carry));
  somador_completo somador_completo_2 (
    .A(A2), .B(B2), .Cin(somador_completo_carry), .Soma(S2), .Carry(somador_completo_2_carry));
  somador_completo somador_completo_3 (.A(A3), .B(B3), .Cin(somador_completo_2_carry), .Soma(S3), .Carry(Carry));
endmodule

module comparador (
  input  B,
  input  [3:0] A,
  output [3:0] out_3
);

  and and_1 (out_3[3], B, A[3]);
  and and_2 (out_3[2], B, A[2]);
  and and_3 (out_3[1], B, A[1]);
  and and_4 (out_3[0], B, A[0]);
endmodule

module multiplicador (
  input  [3:0] B,
  input  [3:0] A,
  output [7:0] out_3
);

  wire [3:0] comparador_2_out_3, comparador_3_out_3, comparador_4_out_3;
  wire [3:1] comparador_1_out_3, somador_1_s, somador_2_s;
  wire [3:3] somador_1_carry, somador_2_carry;

  comparador comparador_1 (.B(B[0]), .A(A), .out_3({comparador_1_out_3, out_3[0]}));
  comparador comparador_2 (.B(B[1]), .A(A), .out_3(comparador_2_out_3));
  comparador comparador_3 (.B(B[2]), .A(A), .out_3(comparador_3_out_3));
  comparador comparador_4 (.B(B[3]), .A(A), .out_3(comparador_4_out_3));
  somador somador_1 (
    .A({1'b0, comparador_1_out_3}), .B(comparador_2_out_3), .Carry(somador_1_carry[3]),
    .S({somador_1_s, out_3[1]}));
  somador somador_2 (
    .A({somador_1_carry[3], somador_1_s}), .B(comparador_3_out_3), .Carry(somador_2_carry[3]),
    .S({somador_2_s, out_3[2]}));
  somador somador_3 (.A({somador_2_carry[3], somador_2_s}), .B(comparador_4_out_3), .Carry(out_3[7]), .S(out_3[6:3]));
endmodule

module divisor (
  input  [3:0] A,
  input  [3:0] B,
  output [3:0] S
);

  Register #(.width(4)) register_1 ();  // open: D, en, Q, clk, clr
  subtrator subtrator_1 (.A(A), .B(B));  // open: Carry, S
  contador contador (.S(S));  // open: CLK
endmodule

module contador (
  input  CLK,
  output [3:0] S
);

  wire and_1_out, and_2_out;

  T_Flip_Flop t_ff_1 (.clk(CLK), .Q(S[3]));  // open: T, Qn, preset, reset, en
  T_Flip_Flop t_ff_2 (.clk(CLK), .T(S[3]), .Q(S[2]));  // open: Qn, preset, reset, en
  and and_1 (and_1_out, S[3], S[2]);
  T_Flip_Flop t_ff_3 (.clk(CLK), .T(and_1_out), .Q(S[1]));  // open: Qn, preset, reset, en
  and and_2 (and_2_out, and_1_out, S[1]);
  T_Flip_Flop t_ff_4 (.clk(CLK), .T(and_2_out), .Q(S[0]));  // open: Qn, preset, reset, en
endmodule

module calculadora (
  input  [3:0] A,
  input  [3:0] B,
  input  [1:0] \Operação ,
  output [7:0] Resultado
);

  wire [3:0] divisor_1_s, somador_1_s, subtrator_1_s;
  wire [4:4] somador_1_carry;
  wire [7:0] and_1_out, and_2_out, and_3_out, and_4_out, multiplicador_1_out_3, not_1_out, not_2_out,
       not_3_out, not_4_out;

  somador somador_1 (.A(A), .B(B), .Carry(somador_1_carry[4]), .S(somador_1_s));
  subtrator subtrator_1 (.A(A), .B(B), .S(subtrator_1_s));  // open: Carry
  multiplicador multiplicador_1 (.B(A), .A(B), .out_3(multiplicador_1_out_3));
  divisor divisor_1 (.A(A), .B(B), .S(divisor_1_s));
  assign and_1_out = {3'b000, somador_1_carry[4], somador_1_s} & not_1_out & not_2_out;  // AND_Gate and_1, 8 bits wide
  assign not_1_out = ~{8{\Operação [0]}};  // NOT_Gate not_1, 8 bits wide
  assign not_2_out = ~{8{\Operação [1]}};  // NOT_Gate not_2, 8 bits wide
  assign and_2_out = {4'b0000, subtrator_1_s} & {8{\Operação [0]}} & not_3_out;  // AND_Gate and_2, 8 bits wide
  assign not_3_out = ~{8{\Operação [1]}};  // NOT_Gate not_3, 8 bits wide
  assign and_3_out = multiplicador_1_out_3 & not_4_out & {8{\Operação [1]}};  // AND_Gate and_3, 8 bits wide
  assign not_4_out = ~{8{\Operação [0]}};  // NOT_Gate not_4, 8 bits wide
  assign and_4_out = {4'b0000, divisor_1_s} & {8{\Operação [0]}} & {8{\Operação [1]}};  // AND_Gate and_4, 8 bits wide
  assign Resultado = and_1_out | and_2_out | and_3_out | and_4_out;  // OR_Gate or_1, 8 bits wide
endmodule

module decodificador_BCD (
  input  [7:0] Entrada,
  output [3:0] S0,
  output [3:0] S1,
  output [3:0] S2
);

  add3 add3_1 ();  // open: in_1, out_2
endmodule

module decodificador_7_seg (
  input  [3:0] Entrada,
  output [6:0] S
);
endmodule

module decodificador_binario_7_seg (
  input  [7:0] Entrada,
  output [6:0] S0,
  output [6:0] S1,
  output [6:0] S2
);

  wire [3:0] decodificador_bcd_s0, decodificador_bcd_s1, decodificador_bcd_s2;

  decodificador_BCD decodificador_bcd (
    .Entrada(Entrada), .S0(decodificador_bcd_s0), .S1(decodificador_bcd_s1), .S2(decodificador_bcd_s2));
  decodificador_7_seg decodificador_7_seg (.Entrada(decodificador_bcd_s0), .S(S0));
  decodificador_7_seg decodificador_7_Seg_2 (.Entrada(decodificador_bcd_s1), .S(S1));
  decodificador_7_seg decodificador_7_seg_3 (.Entrada(decodificador_bcd_s2), .S(S2));
endmodule

module add3 (
  input  [3:0] in_1,
  output [3:0] out_2
);

  wire and_1_out, and_2_out, and_3_out, and_4_out, and_5_out, and_6_out, and_7_out, and_8_out, and_9_out,
       and_10_out, not_1_out, not_2_out, not_3_out, not_4_out, not_5_out, not_6_out, not_7_out, not_8_out;

  not not_1 (not_1_out, in_1[3]);
  and and_1 (and_1_out, not_1_out, not_2_out, in_1[0]);
  not not_2 (not_2_out, in_1[2]);
  and and_2 (and_2_out, in_1[3], in_1[2], not_3_out);
  not not_3 (not_3_out, in_1[0]);
  and and_3 (and_3_out, in_1[2], in_1[1], not_4_out);
  not not_4 (not_4_out, in_1[0]);
  not not_5 (not_5_out, in_1[2]);
  and and_4 (and_4_out, not_5_out, in_1[1]);
  and and_5 (and_5_out, in_1[1], in_1[0]);
  and and_6 (and_6_out, in_1[3], not_6_out);
  not not_6 (not_6_out, in_1[0]);
  and and_7 (and_7_out, in_1[2], not_7_out, not_8_out);
  not not_7 (not_7_out, in_1[1]);
  not not_8 (not_8_out, in_1[0]);
  and and_8 (and_8_out, in_1[3], in_1[0]);
  and and_9 (and_9_out, in_1[2], in_1[1]);
  and and_10 (and_10_out, in_1[2], in_1[0]);
  or or_1 (out_2[0], and_1_out, and_2_out, and_3_out);
  or or_2 (out_2[1], and_4_out, and_5_out, and_6_out);
  or or_3 (out_2[2], and_7_out, and_8_out);
  or or_4 (out_2[3], and_9_out, in_1[3], and_10_out);
endmodule
